# Fritzing sketch HypnoLight (saved by Fritzing 0.9.5d)

parts:
  M1 = ESP32-S3-DevKitC-1-N8R8-v1 [part_number=ESP32-S3-DevKitC-1-N8R8-v1]
  J1 = Screw terminal - 2 pins [package=THT]
  M2 = MT3608 Module
  M3 = MT3608 Module
  T1 = TMP36 Temperature Sensor [package="TO92 [THT]"]
  JP1 = Header 4 [package=screwterminal-3.5mm-4_lock]
  JP2 = Header 4 [package=screwterminal-3.5mm-4_lock]
  JS1 = Generic Jumper Shunt
  Power_RGB1 = Prolight RGB 3 Watt Star
  Power_RGB5 = Prolight RGB 3 Watt Star
  Part3 = PicoBuck LED Driver [part_number=COM-11850]
  Power_RGB2 = Prolight RGB 3 Watt Star
  Power_RGB4 = Prolight RGB 3 Watt Star
  Power_RGB9 = Prolight RGB 3 Watt Star
  Power_RGB3 = Prolight RGB 3 Watt Star
  Power_RGB6 = Prolight RGB 3 Watt Star
  Part2 = PicoBuck LED Driver [part_number=COM-11850]
  Part1 = PicoBuck LED Driver [part_number=COM-11850]
  Power_RGB8 = Prolight RGB 3 Watt Star
  Power_RGB7 = Prolight RGB 3 Watt Star
  R2 = Resistor [tolerance=±5% resistance=10k package=THT]
  R3 = Resistor [tolerance=±5% resistance=10k package=THT]
  R4 = Resistor [tolerance=±5% resistance=10k package=THT]
  R5 = Resistor [tolerance=±5% resistance=10k package=THT]
  R1 = Resistor [tolerance=±5% resistance=10k package=THT]

nets:
  N1: M1.pin_1, M1.pin_2, T1.+Vs, JP2.2
  N2: M1.pin_4, Part2.IN1, Part1.IN1, R1.Pin_0
  N3: M1.pin_5, Part3.IN1, Part3.IN2, R3.Pin_0
  N4: M1.pin_6, Part3.IN3, Part2.IN3, R2.Pin_0
  N5: M1.pin_7, Part1.IN2, Part1.IN3, R4.Pin_0
  N6: M1.pin_8, Part2.IN2, R5.Pin_0
  N7: M1.pin_9, T1.Vout
  N8: M1.pin_10, JP1.3
  N9: M1.pin_11, JP1.4
  N10: M1.pin_21, JS1.pin2
  N11: M1.pin_22, M1.pin_44, M2.pin4, T1.GND, JP2.1, R2.Pin_1, R3.Pin_1, R4.Pin_1, R5.Pin_1, R1.Pin_1
  N12: M1.pin_40, JP2.4
  N13: M1.pin_41, JP2.3
  N14: J1.pin1, M2.pin2, M3.pin2, Part3.VIN_+, Part2.VIN_+, Part1.VIN_+
  N15: J1.pin2, M2.pin1, M3.pin1, Part3.VIN_-, Part2.VIN_-, Part1.VIN_-
  N16: M2.pin3, JS1.pin1
  N17: M3.pin3, JP1.2
  N18: M3.pin4, JP1.1
  N19: Power_RGB1.R+, Part1.OUT3+
  N20: Power_RGB1.R-, Part1.OUT3-
  N21: Power_RGB5.R+, Part2.OUT1+
  N22: Power_RGB5.R-, Part2.OUT1-
  N23: Part3.OUT1+, Power_RGB8.R+
  N24: Part3.OUT1-, Power_RGB8.R-
  N25: Part3.OUT2+, Power_RGB7.R+
  N26: Part3.OUT2-, Power_RGB7.R-
  N27: Part3.OUT3+, Power_RGB9.R+
  N28: Part3.OUT3-, Power_RGB9.R-
  N29: Power_RGB2.R+, Part1.OUT1+
  N30: Power_RGB2.R-, Part1.OUT1-
  N31: Power_RGB4.R+, Part2.OUT2+
  N32: Power_RGB4.R-, Part2.OUT2-
  N33: Power_RGB3.R+, Part1.OUT2+
  N34: Power_RGB3.R-, Part1.OUT2-
  N35: Power_RGB6.R+, Part2.OUT3+
  N36: Power_RGB6.R-, Part2.OUT3-

custom parts:
  ESP32-S3-DevKitC-1-N8R8-v1: ESP32-S3-DevKitC-1-N8R8-v1 This module is 44pins long (2x22) and 11 pins width.
  MT3608 Module: MT3608 Boost Converter Module Links: Aerosemi MT3608 2A Step Up Converter datasheet
  PicoBuck LED Driver: The PicoBuck LED Driver is an economical and easy to use driver that will allow you to control and blend three different LEDs on three different channels. Power in supplied to the PicoBuck with a wide range of input voltages (6v to 20v) connected to the VIN header and three inputs for each driver channel (labeled IN1, IN2, and IN3) driven with standard 3.3v or 5v logic. This PicoBuck supports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
